# Fritzing sketch 52Can (saved by Fritzing 1.0.7)
circuit board: 4.99999cm x 4.99999cm
breadboards: 1

parts:
  U12 = Header 12 [package=1x12_machine-pin-header_lock.004]
  U17 = Header 12 [package=1x12_machine-pin-header_lock.004]
  U16 = Header 12 [package=1x12_machine-pin-header_lock.004]
  U18 = Header 12 [package=1x12_machine-pin-header_lock.004]
  U11 = Header 12 [package=1x12_machine-pin-header_lock.004]
  U13 = Header 12 [package=1x12_machine-pin-header_lock.004]
  U00 = Header 12 [package=1x12_machine-pin-header_lock.004]
  U14 = Header 12 [package=1x12_machine-pin-header_lock.004]
  U15 = Header 12 [package=1x12_machine-pin-header_lock.004]
  U19 = Header 12 [package=1x12_machine-pin-header_lock.004]

nets:
  N1: U12.1, U11.1, U13.1, U14.1
  N2: U12.2, U11.2, U13.2, U14.2
  N3: U12.3, U11.3, U13.3, U14.3
  N4: U12.4, U11.4, U13.4, U14.4
  N5: U12.5, U11.5, U13.5, U14.5
  N6: U12.6, U11.6, U13.6, U14.6
  N7: U12.7, U11.7, U13.7, U14.7
  N8: U12.8, U11.8, U13.8, U14.8
  N9: U12.9, U11.9, U13.9, U14.9
  N10: U12.10, U11.10, U13.10, U14.10
  N11: U12.11, U11.11, U13.11, U14.11
  N12: U12.12, U11.12, U13.12, U14.12
  N13: U17.1, U16.1, U18.1, U15.1, U19.1
  N14: U17.2, U16.2, U18.2, U15.2, U19.2
  N15: U17.3, U16.3, U18.3, U15.3, U19.3
  N16: U17.4, U16.4, U18.4, U15.4, U19.4
  N17: U17.5, U16.5, U18.5, U15.5, U19.5
  N18: U17.6, U16.6, U18.6, U15.6, U19.6
  N19: U17.7, U16.7, U18.7, U15.7, U19.7
  N20: U17.8, U16.8, U18.8, U15.8, U19.8
  N21: U17.9, U16.9, U18.9, U15.9, U19.9
  N22: U17.10, U16.10, U18.10, U15.10, U19.10
  N23: U17.11, U16.11, U18.11, U15.11, U19.11
  N24: U17.12, U16.12, U18.12, U15.12, U19.12
  N25: U00.1, U00.2, U00.3
  N26: U00.9, U00.10, U00.11, U00.12
